# Fritzing sketch Respfritz (saved by Fritzing 0.9.3b)
breadboards: 1

parts:
  Part1 = Arduino Mega ADK (Rev3)
  POT1 = POT [package=pot_mammoth]
  POT2 = POT [package=pot_alpha_rv16af-20]
  POT3 = POT [package=pot_alpha_rv16af-20]
  POT4 = POT [package=pot_alpha_rv16af-20]
  M1 = Stepper Motor - Bipolar
  Part2 = EasyDriver_v44
  V1 = DC Power [voltage=12V]
  S3 = Pushbutton [package="[THT]"]
  S4 = Pushbutton [package="[THT]"]
  LCD2004-I2C1 = LCD2004-I2C
  Part3 = HX711 Weighing Sensor Module
  Pressure_Sensor = Load Cell - Red/white/black/green
  MPXV7002_Pressure_Sensor1 = MPXV7002 Integrated Silicon Pressure Sensor

nets:
  N1: Part1.A0, POT1.A
  N2: Part1.A1, POT2.S
  N3: Part1.A2, POT3.S
  N4: Part1.A3, POT4.S
  N5: Part1.A5, MPXV7002_Pressure_Sensor1.ANALOG
  N6: Part1.D21/SCL, LCD2004-I2C1.SCL
  N7: Part1.D20/SDA, LCD2004-I2C1.SDA
  GND: Part1.GND, POT1.E, POT2.E, POT3.E, POT4.E, Part2.GND, S3.Pin_4, S4.Pin_4, LCD2004-I2C1.GND, Part3.GND, MPXV7002_Pressure_Sensor1.GND
  N8: Part1.D9_PWM, Part3.CK/TX
  N9: Part1.D8_PWM, Part3.DO/RX
  VCC: Part1.5V, POT1.S, POT2.A, POT3.A, POT4.A, LCD2004-I2C1.VCC, Part3.VCC
  N10: Part1.D2_PWM, S4.Pin_1, S4.Pin_2
  N11: Part1.D3_PWM, S3.Pin_1, S3.Pin_2
  N12: Part1.D5_PWM, Part2.DIR
  N13: Part1.D6_PWM, Part2.STEP
  N14: M1.A, Part2.OUT2A
  N15: M1.C, Part2.OUT2B
  N16: M1.B, Part2.OUT1A
  N17: M1.D, Part2.OUT1B
  N18: Part2.VCC, V1.V+
  N19: Part3.E+, Pressure_Sensor.wire1
  N20: Part3.E-, Pressure_Sensor.wire2
  N21: Part3.A+, Pressure_Sensor.wire3
  N22: Part3.A-, Pressure_Sensor.wire4

custom parts:
  LCD2004-I2C: A standard character display with 4x20 characters. Comes in many colors with LCM2004 IIC attached.
  HX711 Weighing Sensor Module: HX711 is a precision 24-bit analog-to-digital converter (ADC) designed for weigh scales and industrial control applications to interface directly with a bridge sensor.
  Load Cell - Red/white/black/green: A rectangle load cell/weighting pressure Sensor with four wires - Red, white, black, green. Normally corresponding with E+, E-, A+, A- respectively.
  MPXV7002 Integrated Silicon Pressure Sensor: Description: The MPXV7002 piezoresistive transducer is a monolithic silicon pressure sensor manufactured by NXP Semiconductors. The transducer provides am analog output signal that is proportional to the applied pressure. Dimensions: 29mm x 21mm
